# Fritzing sketch main (saved by Fritzing 1.0.1rc)
breadboards: 1

parts:
  A2 = Arduino Nano ESP32
  S2 = Momentary Switch [package=ksa_sealed_tac_switch]
  KY-2 = Keyes Relay [package=THT]
  M2 = DC Motor [voltage_(max)=6V voltage_(min)=3V]
  R5 = Resistor [tolerance=±5% resistance=220 package="0402 [SMD]"]
  Chirp!_Soil_Moisture_Sensor1 = Chirp! Soil Moisture Sensor v2.7.3
  VCC2 = Battery block 9V
  U3 = Voltage Regulator - 5V [package="DPak [SMD]"]
  Grove2 = Grove OLED 128x96

nets:
  N1: A2.Pin_2, KY-2.power, Chirp!_Soil_Moisture_Sensor1.Pin_1, Grove2.VCC
  N2: A2.Pin_4, Chirp!_Soil_Moisture_Sensor1.pin_3
  N3: A2.Pin_8, Grove2.SDA
  N4: A2.Pin_9, Grove2.SCL
  GND: A2.Pin_14, A2.Pin_19, S2.2, KY-2.ground, KY-2.NO, R5.Pin_0, Chirp!_Soil_Moisture_Sensor1.pin_5, VCC2.-, U3.GND, Grove2.GND
  N5: A2.Pin_22, S2.3, R5.Pin_1
  N6: A2.Pin_30, KY-2.signal
  N7: KY-2.C, M2.pin_1
  N8: M2.pin_2, U3.output_voltage
  N9: VCC2.+, U3.input_voltage

notes:
  IN / VCC / GND
  VIN / GND / VOUT
  The actual sensor does not communicate via SPI but returns an analogic value. Consider the "SDA/MOSI" pin as this analog output.
  Water pump

custom parts:
  Arduino Nano ESP32: Arduino® Nano ESP32 smd.
  Keyes Relay: The Keyes 5V relay module is suitable for SCM development, home appliance control. It uses a 5V~12V TIL control signal which can control DC / AC signal.
